# Fritzing sketch circuit (saved by Fritzing 0.9.3b)
breadboards: 1

parts:
  부품1 = Arduino Uno (Rev3)
  VCC1 = 4 x AAA Battery Mount
  J1 = Basic Servo
  J2 = Basic Servo
  J3 = Basic Servo
  J4 = Basic Servo

nets:
  N1: 부품1.D3_PWM, J3.pulse
  N2: 부품1.D4, J4.pulse
  N3: 부품1.D5_PWM, J1.pulse
  N4: 부품1.D6_PWM, J2.pulse
  GND: 부품1.GND, VCC1.-, J1.gnd, J2.gnd, J4.gnd
  VCC: 부품1.VIN, VCC1.+, J1.vcc, J2.vcc, J3.vcc, J4.vcc
